# Fritzing sketch ESPGPT (saved by Fritzing 1.0.4)
circuit board: 6.73379cm x 8.36259cm

parts:
  Part1 = Adafruit MAX98357A I2S 3W Class D Amplifier [part_number="Adafruit #3006"]
  Part2 = INMP441
  A1 = Micro SD card reader
  S1 = Tactile switch 12mm [package=THT]
  R1 = Resistor [tolerance=±5% power=0.25W resistance=220 package=THT]
  MH-ET_Live_Minikit_for_ESP1 = MH-ET Live Minikit for ESP32
  VCC1 = Battery [internal_resistance=0.1Ω]
  LED2 = LED - 5mm [color="Red (633nm)" current=0.030A package="5 mm [THT]"]

nets:
  VIN: Part1.VIN, Part2.VDD, A1.Pin_1, MH-ET_Live_Minikit_for_ESP1.3.3V
  GND: Part1.GND, Part1.GAIN, Part2.L/R, Part2.GND, A1.Pin_6, S1.3, S1.4, R1.Pin_0, MH-ET_Live_Minikit_for_ESP1.GND, VCC1.-
  N1: Part1.DIN, MH-ET_Live_Minikit_for_ESP1.TDI
  N2: Part1.BCLK, Part2.SCK, MH-ET_Live_Minikit_for_ESP1.IO32
  N3: Part1.LRCLK, Part2.WS, MH-ET_Live_Minikit_for_ESP1.IO27
  N4: Part2.SD, MH-ET_Live_Minikit_for_ESP1.IO26
  N5: A1.Pin_2, MH-ET_Live_Minikit_for_ESP1.IO5
  N6: A1.Pin_3, MH-ET_Live_Minikit_for_ESP1.IO23
  N7: A1.Pin_4, MH-ET_Live_Minikit_for_ESP1.IO19
  N8: A1.Pin_5, MH-ET_Live_Minikit_for_ESP1.IO18
  N9: S1.1, S1.2, MH-ET_Live_Minikit_for_ESP1.IO17
  N10: R1.Pin_1, LED2.cathode
  N11: MH-ET_Live_Minikit_for_ESP1.IO33, LED2.anode
  N12: MH-ET_Live_Minikit_for_ESP1.VCC, VCC1.+

custom parts:
  Adafruit MAX98357A I2S 3W Class D Amplifier: Listen to this good news - we now have an all in one digital audio amp breakout board that works incredibly well with the Raspberry Pi! If you're looking for an easy and low cost way to get you digital sound files bumpin' then the MAX08357 I2S Amp Breakout is for you. It takes standard I2S digital audio input and, not only decodes it into analog, but also amplifies it directly into a speaker.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
  INMP441: This is a simple breakout board for the INMP441 I2S MEMS microphone.
  Micro SD card reader: Micro SD card reader.
  Tactile switch 12mm: 12 mm tactile switch (push button/momentary switch) from the B3F family.
  MH-ET Live Minikit for ESP32: MH-ET Live Minikit for ESP32 ( http://mh.nodebb.com/topic/8/mh-et-live-minikit-for-esp32/2/) PCB footprint is invalid.
